// Logisim project alu_1bit.circ as structural Verilog: 1 circuit, main circuit ALU_1bit
module ALU_1bit (
  input  A,
  input  B,
  input  Cin,
  input  Op,
  output Cout,
  output Result
);

  wire and_1_out, and_2_out, and_3_out, and_4_out, and_5_out, not_1_out, xor_1_out, xor_2_out, xor_3_out;

  // XOR_Gate xor_1 has open pins: out=xor_1_out
  not not_1 (not_1_out, Op);
  and and_1 (and_1_out, A, B);
  and and_2 (and_2_out, A, B);
  // XOR_Gate xor_2 has open pins: out=xor_2_out
  // XOR_Gate xor_3 has open pins: out=xor_3_out
  and and_3 (and_3_out, and_1_out, Op);
  and and_4 (and_4_out, Cin, xor_2_out);
  and and_5 (and_5_out, xor_3_out, not_1_out);
  or or_1 (Cout, and_2_out, and_4_out);
  or or_2 (Result, and_5_out, and_3_out);
endmodule
