// Logisim project half_adder.circ as structural Verilog: 1 circuit, main circuit Half_Adder
module Half_Adder (
  input  A,
  input  B,
  output Sum,
  output Carry
);

  // XOR_Gate xor_1 has open pins: out=Sum
  and and_1 (Carry, A, B);
endmodule
