// Logisim project mux_4to1.circ as structural Verilog: 1 circuit, main circuit MUX_4to1
module MUX_4to1 (
  input  D0,
  input  D1,
  input  D2,
  input  D3,
  input  S0,
  input  S1,
  output Out
);

  wire and_1_out, and_2_out, and_3_out, and_4_out, and_5_out, and_6_out, and_7_out, and_8_out, not_1_out,
       not_2_out, not_3_out, not_4_out, or_1_out, or_2_out;

  not not_1 (not_1_out, S1);
  not not_2 (not_2_out, S0);
  not not_3 (not_3_out, S1);
  and and_1 (and_1_out, D2, S1);
  not not_4 (not_4_out, S0);
  and and_2 (and_2_out, D3, S1);
  and and_3 (and_3_out, D0, not_1_out);
  and and_4 (and_4_out, D1, not_3_out);
  and and_5 (and_5_out, and_1_out, not_4_out);
  and and_6 (and_6_out, and_2_out, S0);
  and and_7 (and_7_out, and_3_out, not_2_out);
  and and_8 (and_8_out, and_4_out, S0);
  or or_1 (or_1_out, and_7_out, and_8_out);
  or or_2 (or_2_out, or_1_out, and_5_out);
  or or_3 (Out, or_2_out, and_6_out);
endmodule
